# Fritzing sketch Circuit (saved by Fritzing 0.9.10b)

parts:
  U1 = ESP32-38PinWide [part_number=ESP32-38PinWide]
  8x8_LED_Modul_mit_MAX1 = 8x8 LED Modul mit MAX7219 [package=THT]
  8x8_LED_Modul_mit_MAX2 = 8x8 LED Modul mit MAX7219 [package=THT]
  8x8_LED_Modul_mit_MAX3 = 8x8 LED Modul mit MAX7219 [package=THT]
  S1 = Round Pushbutton
  S2 = Round Pushbutton
  S3 = Round Pushbutton

nets:
  N1: U1.GND, 8x8_LED_Modul_mit_MAX1.GND_Eingang, S1.leg0, S2.leg0, S3.leg0
  N2: U1.VIN, 8x8_LED_Modul_mit_MAX1.VCC_Eingang
  N3: U1.GPIO15, 8x8_LED_Modul_mit_MAX1.CS_Eingang
  N4: U1.GPIO0, S1.leg1
  N5: U1.GPIO4, S2.leg1
  N6: U1.GPIO16, S3.leg1
  N7: U1.GPIO18, 8x8_LED_Modul_mit_MAX1.CLK_Eingang
  N8: U1.GPIO23, 8x8_LED_Modul_mit_MAX1.DIN_Eingang
  N9: 8x8_LED_Modul_mit_MAX1.VCC_Ausgang, 8x8_LED_Modul_mit_MAX2.VCC_Eingang
  N10: 8x8_LED_Modul_mit_MAX1.GND_Ausgang, 8x8_LED_Modul_mit_MAX2.GND_Eingang
  N11: 8x8_LED_Modul_mit_MAX1.DOUT_Ausgang, 8x8_LED_Modul_mit_MAX2.DIN_Eingang
  N12: 8x8_LED_Modul_mit_MAX1.CS_Ausgang, 8x8_LED_Modul_mit_MAX2.CS_Eingang
  N13: 8x8_LED_Modul_mit_MAX1.CLK_Ausgang, 8x8_LED_Modul_mit_MAX2.CLK_Eingang
  N14: 8x8_LED_Modul_mit_MAX2.VCC_Ausgang, 8x8_LED_Modul_mit_MAX3.VCC_Eingang
  N15: 8x8_LED_Modul_mit_MAX2.GND_Ausgang, 8x8_LED_Modul_mit_MAX3.GND_Eingang
  N16: 8x8_LED_Modul_mit_MAX2.DOUT_Ausgang, 8x8_LED_Modul_mit_MAX3.DIN_Eingang
  N17: 8x8_LED_Modul_mit_MAX2.CS_Ausgang, 8x8_LED_Modul_mit_MAX3.CS_Eingang
  N18: 8x8_LED_Modul_mit_MAX2.CLK_Ausgang, 8x8_LED_Modul_mit_MAX3.CLK_Eingang

custom parts:
  ESP32-38PinWide: Generic 38-Pin ESP32 with wide format (only access to one side of pins on a breadboard) based on Stephen Lilley's HiLetgo ESP-WROOM-32 ESP32 ESP-32S Development Board.
